# Fritzing sketch Motor_DC (saved by Fritzing 0.9.2b)
breadboards: 1

parts:
  Parte1 = Arduino Uno (Rev3) - ICSP
  Q1 = npn-Powertransistor [package="TO220 [THT]"]
  R1 = Resistor [tolerance=±5% resistance=220 package="1206 [SMD]"]
  M1 = DC Motor

nets:
  N1: Parte1.D9_PWM, R1.Pin_0
  N2: Parte1.GND, Q1.emitter
  N3: Q1.base, R1.Pin_1
  N4: Q1.collector, M1.pin_2

notes:
  12V
  ( + )
  GND
  ( - )
  TIP 41C
  Cooler.
