# Fritzing sketch DHT11 (saved by Fritzing 0.9.2b)
breadboards: 1

parts:
  DHT1 = DHT11 Humitidy and Temperature Sensor
  Parte1 = Arduino Uno (Rev3) - ICSP

nets:
  VDD: DHT1.VDD, Parte1.5V
  N1: DHT1.DATA, Parte1.D3_PWM
  GND: DHT1.GND, Parte1.GND

custom parts:
  DHT11 Humitidy and Temperature Sensor: DHT11 Humidity and Temperature Sensor
